// Logisim project Circuito_Islam_Armani Riti.circ as structural Verilog: 15 circuits, main circuit Main
module Mod_Memory_4_bit (
  input  [3:0] Numero_da_memorizzare,
  input  ck,
  input  Reset,
  output [3:0] out_4
);

  wire [3:0] or_1_out;

  assign or_1_out = out_4 | Numero_da_memorizzare;  // OR_Gate or_1, 4 bits wide
  D_Flip_Flop d_ff_1 (.clk(ck), .D(or_1_out[0]), .Q(out_4[0]), .reset(Reset));  // open: Qn, preset, en
  D_Flip_Flop d_ff_2 (.clk(ck), .D(or_1_out[1]), .Q(out_4[1]), .reset(Reset));  // open: Qn, preset, en
  D_Flip_Flop d_ff_3 (.clk(ck), .D(or_1_out[2]), .Q(out_4[2]), .reset(Reset));  // open: Qn, preset, en
  D_Flip_Flop d_ff_4 (.clk(ck), .D(or_1_out[3]), .Q(out_4[3]), .reset(Reset));  // open: Qn, preset, en
endmodule

module Mod_Memory (
  input  [3:0] Numero_da_salvare,
  input  [3:0] Selector_In_questo_caso__Il_contatore,
  input  Reset,
  input  ck,
  output [3:0] _0,
  output [3:0] _1,
  output [3:0] _2,
  output [3:0] _3,
  output [3:0] _4,
  output [3:0] _5,
  output [3:0] _6,
  output [3:0] _7,
  output [3:0] _8,
  output [3:0] _9,
  output [3:0] _10,
  output [3:0] _11,
  output [3:0] _12,
  output [3:0] _13,
  output [3:0] _14,
  output [3:0] _15
);

  wire [3:0] demultiplexer_1_out0, demultiplexer_1_out1, demultiplexer_1_out2, demultiplexer_1_out3,
       demultiplexer_1_out4, demultiplexer_1_out5, demultiplexer_1_out6, demultiplexer_1_out7,
       demultiplexer_1_out8, demultiplexer_1_out9, demultiplexer_1_out10, demultiplexer_1_out11,
       demultiplexer_1_out12, demultiplexer_1_out13, demultiplexer_1_out14, demultiplexer_1_out15;

  Demultiplexer #(.select(4), .width(4)) demultiplexer_1 (
    .out0(demultiplexer_1_out0), .out1(demultiplexer_1_out1), .out2(demultiplexer_1_out2),
    .out3(demultiplexer_1_out3), .out4(demultiplexer_1_out4), .out5(demultiplexer_1_out5),
    .out6(demultiplexer_1_out6), .out7(demultiplexer_1_out7), .out8(demultiplexer_1_out8),
    .out9(demultiplexer_1_out9), .out10(demultiplexer_1_out10), .out11(demultiplexer_1_out11),
    .out12(demultiplexer_1_out12), .out13(demultiplexer_1_out13), .out14(demultiplexer_1_out14),
    .out15(demultiplexer_1_out15), .in(Numero_da_salvare), .sel(Selector_In_questo_caso__Il_contatore));  // open: en
  Mod_Memory_4_bit mod_memory_4_bit_1 (
    .Numero_da_memorizzare(demultiplexer_1_out0), .ck(ck), .Reset(Reset), .out_4(_0));
  Mod_Memory_4_bit mod_memory_4_bit_2 (
    .Numero_da_memorizzare(demultiplexer_1_out1), .ck(ck), .Reset(Reset), .out_4(_1));
  Mod_Memory_4_bit mod_memory_4_bit_3 (
    .Numero_da_memorizzare(demultiplexer_1_out2), .ck(ck), .Reset(Reset), .out_4(_2));
  Mod_Memory_4_bit mod_memory_4_bit_4 (
    .Numero_da_memorizzare(demultiplexer_1_out3), .ck(ck), .Reset(Reset), .out_4(_3));
  Mod_Memory_4_bit mod_memory_4_bit_5 (
    .Numero_da_memorizzare(demultiplexer_1_out4), .ck(ck), .Reset(Reset), .out_4(_4));
  Mod_Memory_4_bit mod_memory_4_bit_6 (
    .Numero_da_memorizzare(demultiplexer_1_out5), .ck(ck), .Reset(Reset), .out_4(_5));
  Mod_Memory_4_bit mod_memory_4_bit_7 (
    .Numero_da_memorizzare(demultiplexer_1_out6), .ck(ck), .Reset(Reset), .out_4(_6));
  Mod_Memory_4_bit mod_memory_4_bit_8 (
    .Numero_da_memorizzare(demultiplexer_1_out7), .ck(ck), .Reset(Reset), .out_4(_7));
  Mod_Memory_4_bit mod_memory_4_bit_9 (
    .Numero_da_memorizzare(demultiplexer_1_out8), .ck(ck), .Reset(Reset), .out_4(_8));
  Mod_Memory_4_bit mod_memory_4_bit_10 (
    .Numero_da_memorizzare(demultiplexer_1_out9), .ck(ck), .Reset(Reset), .out_4(_9));
  Mod_Memory_4_bit mod_memory_4_bit_11 (
    .Numero_da_memorizzare(demultiplexer_1_out10), .ck(ck), .Reset(Reset), .out_4(_10));
  Mod_Memory_4_bit mod_memory_4_bit_12 (
    .Numero_da_memorizzare(demultiplexer_1_out11), .ck(ck), .Reset(Reset), .out_4(_11));
  Mod_Memory_4_bit mod_memory_4_bit_13 (
    .Numero_da_memorizzare(demultiplexer_1_out12), .ck(ck), .Reset(Reset), .out_4(_12));
  Mod_Memory_4_bit mod_memory_4_bit_14 (
    .Numero_da_memorizzare(demultiplexer_1_out13), .ck(ck), .Reset(Reset), .out_4(_13));
  Mod_Memory_4_bit mod_memory_4_bit_15 (
    .Numero_da_memorizzare(demultiplexer_1_out14), .ck(ck), .Reset(Reset), .out_4(_14));
  Mod_Memory_4_bit mod_memory_4_bit_16 (
    .Numero_da_memorizzare(demultiplexer_1_out15), .ck(ck), .Reset(Reset), .out_4(_15));

  // Other names for the same wires on the sheet: R = Reset
endmodule

module Mod_Video (
  input  [3:0] _0,
  input  [3:0] _1,
  input  [3:0] _2,
  input  [3:0] _3,
  input  [3:0] _4,
  input  [3:0] _5,
  input  [3:0] _6,
  input  [3:0] _7,
  input  [3:0] _8,
  input  [3:0] _9,
  input  [3:0] Index_selector,
  input  [3:0] _10,
  input  [3:0] _11,
  input  [3:0] _12,
  input  [3:0] _13,
  input  [3:0] _14,
  input  [3:0] _15,
  output [15:0] out2,
  output [15:0] out1,
  output [15:0] out4,
  output [15:0] out3
);

  wire [3:0] multiplexer_1_out;

  Multiplexer #(.select(4), .width(4)) multiplexer_1 (
    .in0(_0), .in1(_1), .in2(_2), .in3(_3), .in4(_4), .in5(_5), .in6(_6), .in7(_7), .in8(_8), .in9(_9),
    .in10(_10), .in11(_11), .in12(_12), .in13(_13), .in14(_14), .in15(_15), .out(multiplexer_1_out),
    .sel(Index_selector));  // open: en
  Decoder #(.select(4), .enable("false")) decoder_1 (
    .out0(out1[15]), .out1(out1[11]), .out2(out1[7]), .out3(out1[3]), .out4(out2[15]), .out5(out2[11]),
    .out6(out2[7]), .out7(out2[3]), .out8(out3[15]), .out9(out3[11]), .out10(out3[7]), .out11(out3[3]),
    .out12(out4[15]), .out13(out4[11]), .out14(out4[7]), .out15(out4[3]), .sel(multiplexer_1_out));

  assign {out1[14:12], out1[10:8], out1[6:4], out1[2:0]} = {{3{out1[15]}}, {3{out1[11]}}, {3{out1[7]}}, {3{out1[3]}}};
  assign {out2[14:12], out2[10:8], out2[6:4], out2[2:0]} = {{3{out2[15]}}, {3{out2[11]}}, {3{out2[7]}}, {3{out2[3]}}};
  assign {out3[14:12], out3[10:8], out3[6:4], out3[2:0]} = {{3{out3[15]}}, {3{out3[11]}}, {3{out3[7]}}, {3{out3[3]}}};
  assign {out4[14:12], out4[10:8], out4[6:4], out4[2:0]} = {{3{out4[15]}}, {3{out4[11]}}, {3{out4[7]}}, {3{out4[3]}}};

  // Other names for the same wires on the sheet: Out1_t[3:0] = {out1[3], out1[7], out1[11], out1[15]};
  //   Out2_t[3:0] = {out2[3], out2[7], out2[11], out2[15]}; Out3_t[3:0] = {out3[3], out3[7], out3[11], out3[15]};
  //   Out4_t[3:0] = {out4[3], out4[7], out4[11], out4[15]}
endmodule

module Mod_Random (
  input  ck,
  output [3:0] Numero_random_generato_in_binary
);

  Random #(.width(4)) random_1 (.clk(ck), .next(ck), .out(Numero_random_generato_in_binary));  // open: clr
endmodule

module Mod_Round_control (
  input  ck,
  input  Reset,
  output [3:0] Indice_N_Generato
);

  Counter #(.width(4), .max('hf), .ongoal("stay")) counter_1 (
    .Q(Indice_N_Generato), .clk(ck), .clr(Reset));  // open: load, D, count, carry
endmodule

module Mod_Video_control (
  input  [3:0] N_di_round,
  input  surrend,
  input  ck,
  input  Reset,
  input  again,
  output [3:0] Numero_da_replicare,
  output mostra_a_video,
  output finito_di_mostrare
);

  wire and_1_out, and_2_out, and_3_out, or_1_out;
  wire [3:0] counter_1_q;

  and and_1 (and_1_out, ck, ~again);  // AND_Gate
  Counter #(.width(4), .max('hf), .ongoal("stay")) counter_1 (
    .Q(counter_1_q), .clk(and_2_out), .clr(or_1_out));  // open: load, D, count, carry
  or or_1 (or_1_out, Reset, again);
  and and_2 (and_2_out, and_1_out, ~finito_di_mostrare);  // AND_Gate
  Subtractor #(.width(4)) subtractor_1 (.a(counter_1_q), .b(4'b0001), .out(Numero_da_replicare));  // open: bin, bout
  Comparator #(.width(4), .mode("unsigned")) comparator_1 (
    .a(counter_1_q), .b(N_di_round), .gt(finito_di_mostrare));  // open: eq, lt
  and and_3 (and_3_out, 1'b1, ~again);  // AND_Gate
  or or_2 (mostra_a_video, and_3_out, surrend);
endmodule

module Mod_Generazione (
  input  ck,
  input  reset,
  output fine
);

  wire not_1_out;
  wire [4:0] adder_1_out, register_1_q;

  Register #(.width(5)) register_1 (.D(adder_1_out), .en(not_1_out), .Q(register_1_q), .clk(ck), .clr(reset));
  not not_1 (not_1_out, fine);
  Comparator #(.width(5), .mode("unsigned")) comparator_1 (.a(adder_1_out), .b(5'b10010), .eq(fine));  // open: gt, lt
  Adder #(.width(5)) adder_1 (.a(5'b00001), .b(register_1_q), .out(adder_1_out));  // open: cin, cout
endmodule

module Mod_Round (
  input  prossimo,
  input  reset,
  output [3:0] round_attuale
);

  wire [3:0] counter_1_q;

  Counter #(.width(4), .max('hc), .ongoal("stay")) counter_1 (
    .Q(counter_1_q), .clk(prossimo), .clr(reset));  // open: load, D, count, carry
  Adder #(.width(4)) adder_1 (.a(counter_1_q), .b(4'b0011), .out(round_attuale));  // open: cin, cout
endmodule

module Mod_Buttons (
  input  b1,
  input  b2,
  input  b3,
  input  b4,
  input  b5,
  input  b6,
  input  b7,
  input  b8,
  input  b9,
  input  b10,
  input  b11,
  input  b12,
  input  b13,
  input  b14,
  input  b15,
  input  b16,
  output click,
  output [3:0] Dato_scelto
);

  wire or_2_out;

  or or_1 (click, b1, b2, b3, b4, b5, b6, b7, b8, b9, b10, b11, b12, b13, b14, b15, b16);
  assign Dato_scelto = or_2_out ? 4'b0000 : 4'bz;  // Controlled_Buffer controlled_buffer_1
  or or_2 (or_2_out, ~click, b1);  // OR_Gate
  assign Dato_scelto = b2 ? 4'b0001 : 4'bz;  // Controlled_Buffer controlled_buffer_2
  assign Dato_scelto = b3 ? 4'b0010 : 4'bz;  // Controlled_Buffer controlled_buffer_3
  assign Dato_scelto = b4 ? 4'b0011 : 4'bz;  // Controlled_Buffer controlled_buffer_4
  assign Dato_scelto = b5 ? 4'b0100 : 4'bz;  // Controlled_Buffer controlled_buffer_5
  assign Dato_scelto = b6 ? 4'b0101 : 4'bz;  // Controlled_Buffer controlled_buffer_6
  assign Dato_scelto = b7 ? 4'b0110 : 4'bz;  // Controlled_Buffer controlled_buffer_7
  assign Dato_scelto = b8 ? 4'b0111 : 4'bz;  // Controlled_Buffer controlled_buffer_8
  assign Dato_scelto = b9 ? 4'b1000 : 4'bz;  // Controlled_Buffer controlled_buffer_9
  assign Dato_scelto = b10 ? 4'b1001 : 4'bz;  // Controlled_Buffer controlled_buffer_10
  assign Dato_scelto = b11 ? 4'b1010 : 4'bz;  // Controlled_Buffer controlled_buffer_11
  assign Dato_scelto = b12 ? 4'b1011 : 4'bz;  // Controlled_Buffer controlled_buffer_12
  assign Dato_scelto = b13 ? 4'b1100 : 4'bz;  // Controlled_Buffer controlled_buffer_13
  assign Dato_scelto = b14 ? 4'b1101 : 4'bz;  // Controlled_Buffer controlled_buffer_14
  assign Dato_scelto = b15 ? 4'b1110 : 4'bz;  // Controlled_Buffer controlled_buffer_15
  assign Dato_scelto = b16 ? 4'b1111 : 4'bz;  // Controlled_Buffer controlled_buffer_16
endmodule

module Mod_Check (
  input  [3:0] _0,
  input  [3:0] _1,
  input  finito_di_mostrare,
  input  [3:0] _2,
  input  [3:0] _3,
  input  [3:0] dato_inserito,
  input  [3:0] _4,
  input  click,
  input  [3:0] _5,
  input  [3:0] _6,
  input  [3:0] _7,
  input  [3:0] _8,
  input  [3:0] _9,
  input  [3:0] round_attuale,
  input  [3:0] _10,
  input  [3:0] _11,
  input  [3:0] _12,
  input  [3:0] _13,
  input  [3:0] _14,
  input  ck,
  input  [3:0] _15,
  output prossimo,
  output correct
);

  wire and_1_out, and_3_out, avanti, comparator_2_eq;
  wire [3:0] counter_2_q, Dato_da_indovinare, index;

  and and_1 (and_1_out, click, ck, avanti);
  and and_2 (prossimo, finito_di_mostrare, comparator_2_eq);
  and and_3 (and_3_out, click, ck, avanti);
  Counter #(.width(4), .max('hf)) counter_1 (
    .Q(index), .clk(and_1_out), .clr(prossimo));  // open: load, D, count, carry
  Counter #(.width(4), .max('hf), .ongoal("load")) counter_2 (
    .load(1'b1), .D(round_attuale), .Q(counter_2_q), .clk(and_3_out), .clr(prossimo));  // open: count, carry
  Comparator #(.width(4), .mode("unsigned")) comparator_1 (
    .a(dato_inserito), .b(Dato_da_indovinare), .eq(correct));  // open: gt, lt
  Comparator #(.width(4), .mode("unsigned")) comparator_2 (
    .a(counter_2_q), .b(4'b0001), .eq(comparator_2_eq));  // open: gt, lt
  and and_4 (avanti, finito_di_mostrare, correct);
  Multiplexer #(.select(4), .width(4)) multiplexer_1 (
    .in0(_0), .in1(_1), .in2(_2), .in3(_3), .in4(_4), .in5(_5), .in6(_6), .in7(_7), .in8(_8), .in9(_9),
    .in10(_10), .in11(_11), .in12(_12), .in13(_13), .in14(_14), .in15(_15), .out(Dato_da_indovinare),
    .sel(index));  // open: en

  // Other names for the same wires on the sheet: dato[3:0] = dato_inserito; mostrare = finito_di_mostrare

  // Notes on the sheet:
  //   e
endmodule

module Mod_AllModules (
  input  clock,
  input  reset,
  input  click,
  input  [3:0] round_da_giocare,
  input  [3:0] Dato_utente,
  input  again,
  output [15:0] T1Modified,
  output [3:0] indice_generazione,
  output [15:0] T2Modified,
  output [3:0] vita_attuale,
  output [15:0] T3Modified,
  output [15:0] T4Modified,
  output [3:0] round_attuale,
  output correct,
  output g_fine
);

  wire and_1_out, and_2_out, and_3_out, and_5_out, comparator_1_eq, counter_1_carry, counter_2_carry,
       finito_di_mostrare, mod_life_1_block, mostra_a_video, or_1_out, prossimo, surrend, win;
  wire [2:0] mod_life_1_vita_rimasta;
  wire [3:0] mod_memory_1__0, mod_memory_1__1, mod_memory_1__2, mod_memory_1__3, mod_memory_1__4,
       mod_memory_1__5, mod_memory_1__6, mod_memory_1__7, mod_memory_1__8, mod_memory_1__9, mod_memory_1__10,
       mod_memory_1__11, mod_memory_1__12, mod_memory_1__13, mod_memory_1__14, mod_memory_1__15,
       mod_memory_2__0, mod_memory_2__1, mod_memory_2__2, mod_memory_2__3, mod_memory_2__4, mod_memory_2__5,
       mod_memory_2__6, mod_memory_2__7, mod_memory_2__8, mod_memory_2__9, mod_memory_2__10,
       mod_memory_2__11, mod_memory_2__12, mod_memory_2__13, mod_memory_2__14, mod_memory_2__15, N_Generato,
       round_attuale_t, round_da_mostrare;
  wire [15:0] and_6_out, and_7_out, and_8_out, and_9_out, bit_extender_1_out, bit_extender_2_out,
       g_fine_enlarge, mod_video_1_out1, mod_video_1_out2, mod_video_1_out3, mod_video_1_out4,
       multiplexer_1_out, multiplexer_2_out, multiplexer_3_out, multiplexer_4_out, multiplexer_5_out,
       multiplexer_6_out, multiplexer_7_out, multiplexer_8_out;

  Mod_Memory mod_memory_1 (
    .Numero_da_salvare(N_Generato), .Selector_In_questo_caso__Il_contatore(indice_generazione),
    .Reset(reset), .ck(clock), ._0(mod_memory_1__0), ._1(mod_memory_1__1), ._2(mod_memory_1__2),
    ._3(mod_memory_1__3), ._4(mod_memory_1__4), ._5(mod_memory_1__5), ._6(mod_memory_1__6),
    ._7(mod_memory_1__7), ._8(mod_memory_1__8), ._9(mod_memory_1__9), ._10(mod_memory_1__10),
    ._11(mod_memory_1__11), ._12(mod_memory_1__12), ._13(mod_memory_1__13), ._14(mod_memory_1__14),
    ._15(mod_memory_1__15));
  Mod_Generazione mod_generazione_1 (.ck(clock), .fine(g_fine), .reset(reset));
  Mod_Check mod_check_1 (
    ._0(mod_memory_1__0), ._1(mod_memory_1__1), .finito_di_mostrare(finito_di_mostrare),
    ._2(mod_memory_1__2), ._3(mod_memory_1__3), .dato_inserito(Dato_utente), ._4(mod_memory_1__4),
    ._5(mod_memory_1__5), .click(click), ._6(mod_memory_1__6), ._7(mod_memory_1__7), ._8(mod_memory_1__8),
    ._9(mod_memory_1__9), ._10(mod_memory_1__10), ._11(mod_memory_1__11), ._12(mod_memory_1__12),
    ._13(mod_memory_1__13), ._14(mod_memory_1__14), ._15(mod_memory_1__15), .prossimo(prossimo),
    .round_attuale(round_attuale_t), .correct(correct), .ck(clock));
  and and_1 (and_1_out, clock, ~g_fine);  // AND_Gate
  Mod_Random mod_random_1 (.ck(and_1_out), .Numero_random_generato_in_binary(N_Generato));
  Mod_Round_control mod_round_control_1 (.ck(and_1_out), .Reset(reset), .Indice_N_Generato(indice_generazione));
  and and_2 (and_2_out, g_fine, ~finito_di_mostrare, clock);  // AND_Gate
  Mod_Round mod_round_1 (.prossimo(prossimo), .reset(reset), .round_attuale(round_attuale_t));
  Counter #(.width(2), .max('h3)) counter_1 (.carry(counter_1_carry), .clk(and_2_out));  // open: load, D, count, Q, clr
  Subtractor #(.width(4)) subtractor_1 (.a(round_attuale_t), .b(4'b0010), .out(round_attuale));  // open: bin, bout
  Counter #(.width(2), .max('h3)) counter_2 (.carry(counter_2_carry), .clk(clock));  // open: load, D, count, Q, clr
  and and_3 (and_3_out, again, ~mod_life_1_block);  // AND_Gate
  Mod_Video_control mod_video_control_1 (
    .N_di_round(round_attuale_t), .ck(counter_1_carry), .Numero_da_replicare(round_da_mostrare),
    .Reset(or_1_out), .mostra_a_video(mostra_a_video), .finito_di_mostrare(finito_di_mostrare),
    .again(and_3_out), .surrend(surrend));
  or or_1 (or_1_out, prossimo, reset);
  assign bit_extender_1_out = {{15{finito_di_mostrare}}, finito_di_mostrare};  // Bit_Extender bit_extender_1
  assign bit_extender_2_out = {{15{counter_2_carry}}, counter_2_carry};  // Bit_Extender bit_extender_2
  Mod_Life mod_life_1 (
    .again(again), .Vita_rimasta(mod_life_1_vita_rimasta), .block(mod_life_1_block), .Surrend(surrend),
    .reset(reset));
  assign g_fine_enlarge = {16{g_fine}} & ~bit_extender_1_out & bit_extender_2_out;  // AND_Gate and_4, 16 bits wide
  assign vita_attuale = {{1{1'b0}}, mod_life_1_vita_rimasta};  // Bit_Extender bit_extender_3
  Comparator #(.width(4)) comparator_1 (.a(round_attuale), .b(round_da_giocare), .eq(comparator_1_eq));  // open: gt, lt
  Counter #(.width(1), .max('h1)) counter_3 (.carry(win), .clk(and_5_out), .clr(reset));  // open: load, D, count, Q
  and and_5 (and_5_out, comparator_1_eq, prossimo);
  Mod_Memory mod_memory_2 (
    .Numero_da_salvare(N_Generato), .Selector_In_questo_caso__Il_contatore(indice_generazione),
    .Reset(reset), .ck(clock), ._0(mod_memory_2__0), ._1(mod_memory_2__1), ._2(mod_memory_2__2),
    ._3(mod_memory_2__3), ._4(mod_memory_2__4), ._5(mod_memory_2__5), ._6(mod_memory_2__6),
    ._7(mod_memory_2__7), ._8(mod_memory_2__8), ._9(mod_memory_2__9), ._10(mod_memory_2__10),
    ._11(mod_memory_2__11), ._12(mod_memory_2__12), ._13(mod_memory_2__13), ._14(mod_memory_2__14),
    ._15(mod_memory_2__15));
  Mod_Video mod_video_1 (
    ._0(mod_memory_2__0), ._1(mod_memory_2__1), ._2(mod_memory_2__2), ._3(mod_memory_2__3),
    ._4(mod_memory_2__4), ._5(mod_memory_2__5), ._6(mod_memory_2__6), ._7(mod_memory_2__7),
    ._8(mod_memory_2__8), ._9(mod_memory_2__9), ._10(mod_memory_2__10), ._11(mod_memory_2__11),
    ._12(mod_memory_2__12), ._13(mod_memory_2__13), ._14(mod_memory_2__14), ._15(mod_memory_2__15),
    .Index_selector(round_da_mostrare), .out2(mod_video_1_out2), .out1(mod_video_1_out1),
    .out4(mod_video_1_out4), .out3(mod_video_1_out3));
  assign and_6_out = mod_video_1_out1 & g_fine_enlarge;  // AND_Gate and_6, 16 bits wide
  assign and_7_out = mod_video_1_out2 & g_fine_enlarge;  // AND_Gate and_7, 16 bits wide
  assign and_8_out = mod_video_1_out3 & g_fine_enlarge;  // AND_Gate and_8, 16 bits wide
  assign and_9_out = mod_video_1_out4 & g_fine_enlarge;  // AND_Gate and_9, 16 bits wide
  Multiplexer #(.width(16)) multiplexer_1 (
    .in0(and_6_out), .in1({16{1'b1}}), .out(multiplexer_1_out), .sel(again));  // open: en
  Multiplexer #(.width(16)) multiplexer_2 (
    .in0(and_7_out), .in1({16{1'b1}}), .out(multiplexer_2_out), .sel(again));  // open: en
  Multiplexer #(.width(16)) multiplexer_3 (
    .in0(and_8_out), .in1({16{1'b1}}), .out(multiplexer_3_out), .sel(again));  // open: en
  Multiplexer #(.width(16)) multiplexer_4 (
    .in0(and_9_out), .in1({16{1'b1}}), .out(multiplexer_4_out), .sel(again));  // open: en
  Multiplexer #(.width(16)) multiplexer_5 (
    .in0(multiplexer_1_out), .in1(16'hf000), .out(multiplexer_5_out), .sel(surrend));  // open: en
  Multiplexer #(.width(16)) multiplexer_6 (
    .in0(multiplexer_2_out), .in1(16'hf000), .out(multiplexer_6_out), .sel(surrend));  // open: en
  Multiplexer #(.width(16)) multiplexer_7 (
    .in0(multiplexer_3_out), .in1(16'hf000), .out(multiplexer_7_out), .sel(surrend));  // open: en
  Multiplexer #(.width(16)) multiplexer_8 (
    .in0(multiplexer_4_out), .in1(16'hfff0), .out(multiplexer_8_out), .sel(surrend));  // open: en
  Multiplexer #(.width(16)) multiplexer_9 (
    .in0(multiplexer_5_out), .in1(16'hf00f), .out(T1Modified), .sel(win));  // open: en
  Multiplexer #(.width(16)) multiplexer_10 (
    .in0(multiplexer_6_out), .in1(16'hf00f), .out(T2Modified), .sel(win));  // open: en
  Multiplexer #(.width(16)) multiplexer_11 (
    .in0(multiplexer_7_out), .in1(16'hf00f), .out(T3Modified), .sel(win));  // open: en
  Multiplexer #(.width(16)) multiplexer_12 (
    .in0(multiplexer_8_out), .in1(16'hff0), .out(T4Modified), .sel(win));  // open: en

  // Other names for the same wires on the sheet: ck = clock; indice_generato[3:0] = indice_generazione;
  //   round_now[3:0] = round_attuale
endmodule

module Mod_LoadingBar (
  input  [3:0] in_1,
  output [15:0] out_2
);

  Multiplexer #(.select(4), .width(16)) multiplexer_1 (
    .in0(16'h8000), .in1(16'h4000), .in2(16'h2000), .in3(16'h1000), .in4(16'h800), .in5(16'h400),
    .in6(16'h200), .in7(16'h100), .in8(16'h80), .in9(16'h40), .in10(16'h20), .in11(16'h10), .in12(16'h8),
    .in13(16'h4), .in14(16'h2), .in15(16'h1), .out(out_2), .sel(in_1));  // open: en
endmodule

module Mod_Life (
  input  again,
  input  reset,
  output [2:0] Vita_rimasta,
  output block,
  output Surrend
);

  wire [2:0] counter_1_q;

  Counter #(.width(3), .max('h3), .ongoal("stay")) counter_1 (
    .Q(counter_1_q), .carry(block), .clk(again), .clr(reset));  // open: load, D, count
  Subtractor #(.width(3)) subtractor_1 (.a(3'b011), .b(counter_1_q), .out(Vita_rimasta));  // open: bin, bout
  Counter #(.width(3), .max('h4), .ongoal("stay")) counter_2 (
    .carry(Surrend), .clk(again), .clr(reset));  // open: load, D, count, Q
endmodule

module Main (
  input  [3:0] round_da_giocare
);

  wire again, B1, B2, B3, B4, B5, B6, B7, B8, B9, Ba, Bb, Bc, Bd, Be, Bf, Bg, ck, Reset;
  wire [3:0] Loading, Round_Now, vita;
  wire [15:0] mod_loadingbar_1_out_2, T1Modified, T2Modified, T3Modified, T4Modified;

  Clock clock_1 (.out(ck));
  Button button_1 (.out(Reset));
  Hex_Digit_Display hex_digit_display_1 (.value(Round_Now));  // open: dp
  Button button_2 (.out(B1));
  Button button_3 (.out(B5));
  Button button_4 (.out(B9));
  Button button_5 (.out(Bd));
  Mod_LoadingBar mod_loadingbar_1 (.in_1(Loading), .out_2(mod_loadingbar_1_out_2));
  DotMatrix #(.inputtype("row"), .matrixcols(16), .matrixrows(1)) dotmatrix_1 (.row0(mod_loadingbar_1_out_2));
  DotMatrix #(.inputtype("row"), .matrixcols(16), .matrixrows(16)) dotmatrix_2 (
    .row0(T1Modified), .row1(T1Modified), .row2(T1Modified), .row3(T1Modified), .row4(T2Modified),
    .row5(T2Modified), .row6(T2Modified), .row7(T2Modified), .row8(T3Modified), .row9(T3Modified),
    .row10(T3Modified), .row11(T3Modified), .row12(T4Modified), .row13(T4Modified), .row14(T4Modified),
    .row15(T4Modified));
  Button button_6 (.out(B2));
  Button button_7 (.out(B6));
  Button button_8 (.out(Ba));
  Button button_9 (.out(Be));
  Button button_10 (.out(B3));
  Button button_11 (.out(B7));
  Button button_12 (.out(Bb));
  Button button_13 (.out(Bf));
  Button button_14 (.out(B4));
  Button button_15 (.out(B8));
  Button button_16 (.out(Bc));
  Button button_17 (.out(Bg));
  Hex_Digit_Display hex_digit_display_2 (.value(vita));  // open: dp
  Button button_18 (.out(again));
  Mod_FullCircuit mod_fullcircuit_1 (
    .clock(ck), .reset(Reset), .round_da_giocare(round_da_giocare), .again(again), .Loading_bar(Loading),
    .round_attuale(Round_Now), .vita_attuale(vita), .b1(B1), .b2(B2), .b3(B3), .b4(B4), .b5(B5), .b6(B6),
    .b7(B7), .b8(B8), .b9(B9), .b10(Ba), .b11(Bb), .b12(Bc), .b13(Bd), .b14(Be), .b15(Bf), .b16(Bg),
    .t1(T1Modified), .t2(T2Modified), .t3(T3Modified), .t4(T4Modified));

  // Other names for the same wires on the sheet: round[3:0] = round_da_giocare

  // Notes on the sheet:
  //   Da 1 a 13
endmodule

// Memory Game
module Mod_FullCircuit (
  input  b1,
  input  b2,
  input  b3,
  input  b4,
  input  b5,
  input  b6,
  input  b7,
  input  b8,
  input  b9,
  input  b10,
  input  b11,
  input  b12,
  input  b13,
  input  b14,
  input  b15,
  input  b16,
  input  clock,
  input  reset,
  input  [3:0] round_da_giocare,
  input  again,
  output [3:0] Loading_bar,
  output [15:0] t1,
  output [15:0] t2,
  output [15:0] t3,
  output [3:0] round_attuale,
  output [15:0] t4,
  output [3:0] vita_attuale
);

  wire click;
  wire [3:0] Dato_scelto_da_utente;

  Mod_AllModules mod_allmodules_1 (
    .clock(clock), .reset(reset), .click(click), .Dato_utente(Dato_scelto_da_utente), .T1Modified(t1),
    .T2Modified(t2), .indice_generazione(Loading_bar), .T3Modified(t3), .T4Modified(t4),
    .round_attuale(round_attuale), .again(again), .vita_attuale(vita_attuale),
    .round_da_giocare(round_da_giocare));  // open: correct, g_fine
  Mod_Buttons mod_buttons_1 (
    .b1(b1), .b2(b2), .b3(b3), .b4(b4), .b5(b5), .b6(b6), .b7(b7), .b8(b8), .b10(b10), .b11(b11), .b12(b12),
    .b13(b13), .b14(b14), .b15(b15), .b16(b16), .Dato_scelto(Dato_scelto_da_utente), .b9(b9), .click(click));

  // Other names for the same wires on the sheet: ck = clock
endmodule
